# Fritzing sketch Sketch (saved by Fritzing 0.9.3b)
circuit board: 8.46667cm x 5.64444cm
stripboards: 1

parts:
  M1 = Raspberry Pi Pico
  DHT1 = DHT22 Humidity and Temperature Sensor
  Part1 = 12 NeoPixel Ring [part_number=1643]
  U1 = Mini-360 DC-DC Buck converter [package=THT]
  J1 = Screw terminal - 2 pins [package=THT]
  R1 = Resistor [tolerance=±5% resistance=1k package="2512 [SMD]"]
  LED1 = RGB LED - (4 legs) [package="5 mm [THT]"]
  D1 = Zener Diode [part_number=1N4732A breakdown_voltage=3.6V package="Melf DO-213 AB [SMD]"]
  Q1 = NPN-Transistor [package="TO92 [THT]"]
  J2 = Screw terminal - 2 pins [package=THT]

nets:
  N1: M1.pin_3, M1.pin_8, M1.pin_13, M1.pin_18, M1.pin_23, M1.pin_28, M1.pin_33, M1.pin_38, M1.pin_42, Part1.GND
  N2: M1.pin_4, DHT1.DATA
  N3: M1.pin_24, R1.Pin_0
  N4: M1.pin_32, Part1.IN
  N5: M1.pin_36, DHT1.VDD
  N6: M1.pin_39, Part1.VDD, D1.cathode
  N7: DHT1.GND, U1.IN-, J1.pin2, LED1.green_cathode
  N8: U1.IN+, J1.pin1, Q1.E
  N9: U1.OUT+, D1.anode
  N10: R1.Pin_1, Q1.B
  N11: LED1.common_anode, Q1.C, J2.pin2

custom parts:
  Raspberry Pi Pico: Raspberry Pi Pico. Based around the RP2040 microcontroller the Pico is a low cost microcontroller device bringing Raspberry Pi quality, cost, and easy of use to the microcontroller space. Jan 2021, Split part in to two versions: SMD (this one) and tht. This one is single sided and uses the castellation pads to solder the module to the board (no holes, other than for the USB connector!). The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
  12 NeoPixel Ring: 12 ultra bright smart LED NeoPixels are arranged in a circle with 1.5" (37mm) outer diameter. The rings are 'chainable' - connect the output pin of one to the input pin of another. Use only one microcontroller pin to control as many as you can chain together! Each LED is addressable as the driver chip is inside the LED. Each one has ~18mA constant current drive so the color will be very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
  Mini-360 DC-DC Buck converter: Mini-360 DC-DC Buck converter. Tiny buck step down voltage converter, input voltage 4.75 to 23V output 1 to 17V adjustable. Available from ebay and the like.
